// Digital circuit Acc8-seq.dig as structural Verilog
module Acc8_seq (
  input  rst,
  input  en,
  input  clk,
  output [7:0] R,
  output OVF
);

  wire acc8_1_ovf, counter_1_ovf;
  wire [3:0] counter_1_out;
  wire [7:0] rom_1_d;

  Counter #(.Bits(4)) counter_1 (.en(en), .C(clk), .clr(rst), .out(counter_1_out), .ovf(counter_1_ovf));
  ROM #(.AddrBits(4), .Bits(8)) rom_1 (.A(counter_1_out), .sel(1'b1), .D(rom_1_d));
  Acc8 acc8_1 (.A(rom_1_d), .en(en), .rst(rst), .clk(clk), .AS(1'b0), .R(R), .OVF(acc8_1_ovf));
  or or_1 (OVF, acc8_1_ovf, counter_1_ovf);

  // Notes on the sheet:
  //   clk: Hz: 50
  //   contents of rom_1 (hex, n*v repeats v):
  //   1,2,3,4,5,6,7,8,9,10,11,12,13,14,15,16
endmodule
