// Digital circuit Acc8.dig as structural Verilog
module Acc8 (
  input  [7:0] A,
  input  en,
  input  rst,
  input  clk,
  input  AS,
  output [7:0] R,
  output OVF
);

  wire [7:0] reg8_1_p2;

  // Reg8 reg8_1: pin names not known; wires that end beside it: clk, reg8_1_p2, rst, en, R
  AddSub8_ovf addsub8_ovf_1 (.A(A), .B(R), .AS(AS), .R(reg8_1_p2), .OVF(OVF));

  // Notes on the sheet:
  //   clk: Hz: 50
endmodule
