// Digital circuit Add8.dig as structural Verilog
module Add8 (
  input  Ci,
  input  [7:0] A0,
  input  [7:0] B0,
  output [7:0] S
);

  wire fa_2_c0, fa_3_c0, fa_4_c0, fa_5_c0, fa_6_c0, fa_7_c0, fa_8_c0;

  FA fa_1 (.A(A0[7]), .B(B0[7]), .Ci(fa_2_c0), .S(S[7]));  // open: C0
  FA fa_2 (.A(A0[6]), .B(B0[6]), .Ci(fa_3_c0), .S(S[6]), .C0(fa_2_c0));
  FA fa_3 (.A(A0[5]), .B(B0[5]), .Ci(fa_4_c0), .S(S[5]), .C0(fa_3_c0));
  FA fa_4 (.A(A0[4]), .B(B0[4]), .Ci(fa_5_c0), .S(S[4]), .C0(fa_4_c0));
  FA fa_5 (.A(A0[3]), .B(B0[3]), .Ci(fa_6_c0), .S(S[3]), .C0(fa_5_c0));
  FA fa_6 (.A(A0[2]), .B(B0[2]), .Ci(fa_7_c0), .S(S[2]), .C0(fa_6_c0));
  FA fa_7 (.A(A0[1]), .B(B0[1]), .Ci(fa_8_c0), .S(S[1]), .C0(fa_7_c0));
  FA fa_8 (.A(B0[0]), .B(A0[0]), .Ci(Ci), .S(S[0]), .C0(fa_8_c0));
endmodule
