// Digital circuit AddSub8-ovf.dig as structural Verilog
module AddSub8_ovf (
  input  [7:0] A,
  input  [7:0] B,
  input  AS,
  output [7:0] R,
  output OVF
);

  AddSub8 addsub8_1 (.B(B), .AS(AS), .A(A), .S(R));
  // det_OVF det_ovf_1: pin names not known; wires that end beside it: AS, A[7], B[7], R[7], OVF
endmodule
