// Digital circuit AddSub8.dig as structural Verilog
module AddSub8 (
  input  [7:0] B,
  input  AS,
  input  [7:0] A,
  output [7:0] S
);

  wire [7:0] xor_1_out;

  assign xor_1_out = {8{AS}} ^ B;  // XOr xor_1, 8 bits wide
  Add8 add8_1 (.Ci(AS), .A0(A), .B0(xor_1_out), .S(S));
endmodule
