// Digital circuit Sys1.dig as structural Verilog
module Sys1 (
  input  A3,
  input  A2,
  input  A1,
  input  A0,
  input  B2,
  input  B3,
  input  B1,
  input  B0,
  output Out
);

  wire BC1_f0, BC1_f1, BC1_f2, BC2_f0, BC2_f1, BC2_f2, xnor_1_out, xnor_2_out, xnor_3_out;

  bitcount BC1 (.X3(A3), .X2(A2), .X1(A1), .X0(A0), .F2(BC1_f2), .F1(BC1_f1), .F0(BC1_f0));
  bitcount BC2 (.X3(B3), .X2(B2), .X1(B1), .X0(B0), .F2(BC2_f2), .F1(BC2_f1), .F0(BC2_f0));
  xnor xnor_1 (xnor_1_out, BC1_f2, BC2_f2);
  xnor xnor_2 (xnor_2_out, BC1_f1, BC2_f1);
  xnor xnor_3 (xnor_3_out, BC1_f0, BC2_f0);
  and and_1 (Out, xnor_1_out, xnor_2_out, xnor_3_out);
endmodule
