// Digital circuit detect.dig as structural Verilog
module detect (
  input  X1,
  input  X4,
  input  X3,
  input  X2,
  output F
);

  wire and_1_out, nor_1_out;

  and and_1 (and_1_out, X1, X2, X3, X4);
  nor nor_1 (nor_1_out, X1, X2, X3, X4);
  or or_1 (F, and_1_out, nor_1_out);
endmodule
